# Fritzing sketch alarmfzz (saved by Fritzing 0.9.2b)
breadboards: 1

parts:
  LCD1 = LCD screen
  Part1 = Arduino Uno (Rev3) - ICSP
  R1 = Resistor [tolerance=±5% resistance=220 package="2512 [SMD]"]
  S1 = Momentary Switch [package=ksa_sealed_tac_switch]
  S2 = Momentary Switch [package=ksa_sealed_tac_switch]
  R2 = Resistor [tolerance=±5% resistance=10k package="2512 [SMD]"]
  R3 = Resistor [tolerance=±5% resistance=10k package="2512 [SMD]"]
  J1 = Piezo Speaker
  R4 = Resistor [tolerance=±5% resistance=1M package="2512 [SMD]"]
  J2 = Piezo Speaker

nets:
  VSS: LCD1.VSS, LCD1.V0, LCD1.R/W, LCD1.LED-, Part1.GND, R2.Pin_0, R3.Pin_0, R4.Pin_1, J2.pin1
  VDD: LCD1.VDD, Part1.5V, R1.Pin_0, S1.1, S2.1, J1.pin2
  N1: LCD1.RS, Part1.ICSP_MISO, Part1.D12/MISO
  N2: LCD1.E, Part1.ICSP_MOSI, Part1.D11_PWM/MOSI
  N3: LCD1.DB4, Part1.D2
  N4: LCD1.DB5, Part1.D3_PWM
  N5: LCD1.DB6, Part1.D4
  N6: LCD1.DB7, Part1.D5_PWM
  N7: LCD1.LED+, R1.Pin_1
  N8: Part1.A0, J1.pin1, R4.Pin_0
  N9: Part1.D8, J2.pin2
  N10: Part1.D6_PWM, S1.3, R2.Pin_1
  N11: Part1.D7, S2.3, R3.Pin_1
